# Fritzing sketch Infrared Test (saved by Fritzing 0.9.3b)
breadboards: 2

parts:
  Part1 = Arduino Uno (Rev3)
  Part2 = KY-005 Infrared Transmitter Module [package="Breakout board"]
  Part3 = Arduino Uno (Rev3)
  Part4 = KY-022 Infrared Receiver Module [package="Breakout board"]
  Part5 = KY-004 Key Switch Module [package="Breakout board"]
  Part6 = KY-009 Full Color RGB LED SMD Module [package="Breakout board"]

nets:
  N1: Part1.D10_PWM/SS, Part5.S
  N2: Part1.D3_PWM, Part2.S
  VIN: Part1.5V, Part2.Vin, Part5.Vin
  N3: Part1.GND, Part2.-, Part5.-
  N4: Part3.D9_PWM, Part6.G
  N5: Part3.D10_PWM/SS, Part6.B
  N6: Part3.D11_PWM/MOSI, Part6.R
  N7: Part3.D13/SCK, Part4.S
  N8: Part3.GND, Part4.-, Part6.-
  5V: Part3.5V, Part4.Vin

custom parts:
  KY-005 Infrared Transmitter Module: Arduino IR Transmitter Module Keyes KY-005, emits infrared light at 38KHz.
  KY-022 Infrared Receiver Module: Arduino IR receiver module KY-022, reacts to 38kHz infrared light.
  KY-004 Key Switch Module: Arduino Key Switch Module Keyes KY-004 is a push button that will output a high signal when pressed.
  KY-009 Full Color RGB LED SMD Module: RGB full color LED Module KY-009 for Arduino, emits a range of colors by mixing red, green and blue. The amount of each primary color is adjusted using PWM.
